# Fritzing sketch card_reader (saved by Fritzing 0.9.2b)
breadboards: 1

parts:
  Bauteil1 = Arduino Uno (Rev3)
  LED1 = LED - 5mm [color="Green (570nm)" package="5 mm [THT]"]
  LED2 = LED - 5mm [color="Red (633nm)" package="5 mm [THT]"]
  R1 = Resistor [tolerance=±5% resistance=220 package=THT]
  R2 = Resistor [tolerance=±5% resistance=220 package=THT]
  Bauteil2 = RFID-RC522-v2

nets:
  N1: Bauteil1.D10_PWM/SS, Bauteil2.SDA
  N2: Bauteil1.D11_PWM/MOSI, Bauteil2.MOSI
  N3: Bauteil1.D12/MISO, Bauteil2.MISO
  N4: Bauteil1.D13/SCK, Bauteil2.SCK
  GND: Bauteil1.GND, R1.Pin_0, R2.Pin_0, Bauteil2.GND
  N5: Bauteil1.D2, LED2.anode
  N6: Bauteil1.D3_PWM, LED1.anode
  N7: Bauteil1.D5_PWM, Bauteil2.RST
  3V3: Bauteil1.3V3, Bauteil2.3.3V
  N8: LED1.cathode, R1.Pin_1
  N9: LED2.cathode, R2.Pin_1

custom parts:
  RFID-RC522-v2: A simple China made RFID-RC522 Reader; do check the pin labels, as this is a MFRC522 based clone.

// code stored in the sketch: meet_up.ino
#include <AddicoreRFID.h>

#include <SPI.h>
#define uchar unsigned char
#define uint unsigned int
//4 bytes tag serial number, the first 5 bytes for the checksum byte
uchar serNumA[5];
//© Addicore LLC 2015 v1.2
uchar fifobytes;
uchar fifoValue;
AddicoreRFID myRFID; // create AddicoreRFID object to control the RFID module
/////////////////////////////////////////////////////////////////////
//set the pins
/////////////////////////////////////////////////////////////////////
const int chipSelectPin = 10;
const int NRSTPD = 5;
const int LED_RED_PIN = 2;
const int LED_GREEN_PIN = 3;
////////////////////////
//Set the occuped state
boolean occupied = false;
///////////////////////
//Maximum length of the array
#define MAX_LEN 16
//////////////////
//HELPER FUNCTIONS
//////////////////
void wirteOccupiedState(boolean occupied) {
  if (occupied) {
    digitalWrite(LED_RED_PIN, HIGH);
    digitalWrite(LED_GREEN_PIN, LOW);
  }
  else {
    digitalWrite(LED_GREEN_PIN, HIGH);
    digitalWrite(LED_RED_PIN, LOW);
  }
}

boolean switchIt(boolean input) {
  return !input;
}

void setup() {
  Serial.begin(9600); // RFID reader SOUT pin connected to Serial RX pin at 9600bps
  // start the SPI library:
  SPI.begin();
  pinMode(LED_RED_PIN, OUTPUT);
  pinMode(LED_GREEN_PIN, OUTPUT);
  pinMode(chipSelectPin, OUTPUT); // Set digital pin 10 as OUTPUT to connect it to the RFID /ENABLE pin
  digitalWrite(chipSelectPin, LOW); // Activate the RFID reader
  pinMode(NRSTPD, OUTPUT); // Set digital pin 10 , Not Reset and Power-down
  digitalWrite(NRSTPD, HIGH);
  myRFID.AddicoreRFID_Init();
  wirteOccupiedState(occupied);
}
void loop()
{
  uchar i, tmp, checksum1;
  uchar status;
  uchar str[MAX_LEN];
  uchar RC_size;
  uchar blockAddr; //Selection operation block address 0 to 63
  String mynum = "";
  str[1] = 0x4400;
  //Find tags, return tag type
  status = myRFID.AddicoreRFID_Request(PICC_REQIDL, str);
  if (status == MI_OK)
  {
    occupied = switchIt(occupied);
    wirteOccupiedState(occupied);
    Serial.println("RFID tag detected");
    Serial.print(str[0], BIN);
    Serial.print(" , ");
    Serial.print(str[1], BIN);
    Serial.println(" ");
  }
  //© Addicore LLC 2015 v1.2
  //Anti-collision, return tag serial number 4 bytes
  status = myRFID.AddicoreRFID_Anticoll(str);
  if (status == MI_OK)
  {

    checksum1 = str[0] ^ str[1] ^ str[2] ^ str[3];
    Serial.println("The tag's number is : ");
    //Serial.print(2);
    Serial.print(str[0]);
    Serial.print(" , ");
    Serial.print(str[1], BIN);
    Serial.print(" , ");
    Serial.print(str[2], BIN);
    Serial.print(" , ");
    Serial.print(str[3], BIN);
    Serial.print(" , ");
    Serial.print(str[4], BIN);
    Serial.print(" , ");
    Serial.println(checksum1, BIN);

    // Should really check all pairs, but for now we'll just use the first
    if (str[0] == 156) //You can change this to the first byte of your tag by finding the card's ID through the Serial Monitor
    {
      Serial.print("Hello Craig!\n");
    } else if (str[0] == 244) { //You can change this to the first byte of your tag by finding the card's ID through the Serial Monitor
      Serial.print("Hello Erin!\n");
    }
    Serial.println();
    delay(1000);
  }
  myRFID.AddicoreRFID_Halt(); //Command tag into hibernation
}
