# Fritzing sketch meet_up (saved by Fritzing 0.9.2b)
breadboards: 1

parts:
  Bauteil1 = Arduino Uno (Rev3)
  LED1 = LED - 5mm [color="Green (570nm)" package="5 mm [THT]"]
  LED2 = LED - 5mm [color="Red (633nm)" package="5 mm [THT]"]
  R1 = Resistor [tolerance=±5% resistance=220 package=THT]
  R2 = Resistor [tolerance=±5% resistance=22 package=THT]

nets:
  N1: Bauteil1.D3_PWM, LED1.cathode, R1.Pin_0
  N2: Bauteil1.GND, LED1.anode, R1.Pin_1
  N3: LED2.cathode, R2.Pin_0
  N4: LED2.anode, R2.Pin_1
