# Fritzing sketch meet_up_lcd (saved by Fritzing 0.9.2b)
breadboards: 1

parts:
  Bauteil1 = Arduino Mega 2560 (Rev3)
  R1 = Rotary Potentiometer (Large) [maximum_resistance=100kΩ package=THT]
  LCD1 = LCD screen
  LED1 = RGB LED (com. cathode, rgb) [package="5 mm [THT]"]
  Bauteil2 = RFID-RC522-v2
  R2 = Resistor [tolerance=±5% resistance=220 package="0805 [SMD]"]
  R3 = Resistor [tolerance=±5% resistance=220 package="0805 [SMD]"]
  R4 = Resistor [tolerance=±5% resistance=220 package="0805 [SMD]"]
  R5 = Resistor [tolerance=±5% resistance=220 package="1206 [SMD]"]

nets:
  GND: Bauteil1.GND, R1.leg2, LCD1.VSS, LCD1.E, LCD1.LED-, Bauteil2.GND
  N1: Bauteil1.D10_PWM, R2.Pin_1
  N2: Bauteil1.D9_PWM, R3.Pin_1
  N3: Bauteil1.D8_PWM, R4.Pin_1
  3V3: Bauteil1.3V3, Bauteil2.3.3V
  5V: Bauteil1.5V, R1.leg1, LCD1.VDD, LED1.red_anode, R5.Pin_1
  N4: Bauteil1.D5_PWM, Bauteil2.RST
  N5: Bauteil1.D38, LCD1.DB0
  N6: Bauteil1.D40, LCD1.R/W
  N7: Bauteil1.D42, LCD1.DB7
  N8: Bauteil1.D44, LCD1.DB6
  N9: Bauteil1.D46, LCD1.DB5
  N10: Bauteil1.D48, LCD1.DB4
  N11: Bauteil1.D50, Bauteil2.MISO
  N12: Bauteil1.D51, Bauteil2.MOSI
  N13: Bauteil1.D52, Bauteil2.SCK
  N14: Bauteil1.D53, Bauteil2.SDA
  N15: R1.wiper, LCD1.V0
  N16: LCD1.LED+, R5.Pin_0
  N17: LED1.common_cathode, R2.Pin_0
  N18: LED1.green_anode, R3.Pin_0
  N19: LED1.blue_anode, R4.Pin_0

custom parts:
  RFID-RC522-v2: A simple China made RFID-RC522 Reader; do check the pin labels, as this is a MFRC522 based clone.
